# Fritzing sketch ArduinoSiren (saved by Fritzing 0.9.3b)
breadboards: 1

parts:
  LED1 = LED - 5mm [color="Red (633nm)" package="5 mm [THT]"]
  LED2 = LED - 5mm [color="Red (633nm)" package="5 mm [THT]"]
  LED3 = LED - 5mm [color="Red (633nm)" package="5 mm [THT]"]
  LED4 = LED - 5mm [color="Red (633nm)" package="5 mm [THT]"]
  LED5 = LED - 5mm [color="Red (633nm)" package="5 mm [THT]"]
  LED6 = LED - 5mm [color="Blue (430nm)" package="5 mm [THT]"]
  LED7 = LED - 5mm [color="Blue (430nm)" package="5 mm [THT]"]
  LED8 = LED - 5mm [color="Blue (430nm)" package="5 mm [THT]"]
  LED9 = LED - 5mm [color="Blue (430nm)" package="5 mm [THT]"]
  LED10 = LED - 5mm [color="Blue (430nm)" package="5 mm [THT]"]
  S1 = Round Pushbutton
  S2 = Momentary Switch [package=ksa_sealed_tac_switch]
  S3 = Momentary Switch [package=ksa_sealed_tac_switch]
  VCC1 = Battery block 9V
  C1 = Capacitor Polarized [package=cpol-radial-10uf-25v]
  C2 = Capacitor Polarized [package=cpol-radial-10uf-25v]
  U1 = atmega328 [package=dip]
  R12 = Resistor [tolerance=±5% resistance=10k package=THT]
  R13 = Resistor [tolerance=±5% resistance=220 package=THT]
  R14 = Resistor [tolerance=±5% resistance=220 package=THT]
  R15 = Resistor [tolerance=±5% resistance=220 package=THT]
  R16 = Resistor [tolerance=±5% resistance=220 package=THT]
  R17 = Resistor [tolerance=±5% resistance=220 package=THT]
  R18 = Resistor [tolerance=±5% resistance=220 package=THT]
  R19 = Resistor [tolerance=±5% resistance=220 package=THT]
  R20 = Resistor [tolerance=±5% resistance=220 package=THT]
  R21 = Resistor [tolerance=±5% resistance=220 package=THT]
  R22 = Resistor [tolerance=±5% resistance=220 package=THT]
  XTAL1 = Crystal [frequency="16 Mhz" package=THT]
  C5 = Ceramic Capacitor [capacitance=22pF package="0805 [SMD, multilayer]"]
  C6 = Ceramic Capacitor [capacitance=22pF package="0805 [SMD, multilayer]"]
  LED11 = LED - 5mm [color="Green (555nm)" package="5 mm [THT]"]
  R23 = Resistor [tolerance=±5% resistance=220 package=THT]
  J1 = Piezo Speaker
  R24 = Resistor [tolerance=±5% resistance=100 package=THT]
  R25 = Resistor [tolerance=±5% resistance=10k package=THT]
  U2 = Voltage Regulator - 5V [package="TO220 [THT]"]

nets:
  N1: LED1.cathode, R13.Pin_0
  N2: LED1.anode, U1.D3_(PWM)
  N3: LED2.cathode, R22.Pin_0
  N4: LED2.anode, U1.D4
  N5: LED3.cathode, R15.Pin_0
  N6: LED3.anode, U1.D5_(PWM)
  N7: LED4.cathode, R16.Pin_0
  N8: LED4.anode, U1.D6_(PWM)
  N9: LED5.cathode, R17.Pin_0
  N10: LED5.anode, U1.D7
  N11: LED6.cathode, R21.Pin_0
  N12: LED6.anode, U1.D11_(PWM)
  N13: LED7.cathode, R14.Pin_0
  N14: LED7.anode, U1.D12
  N15: LED8.cathode, R20.Pin_0
  N16: LED8.anode, U1.D10_(PWM)
  N17: LED9.cathode, R19.Pin_0
  N18: LED9.anode, U1.D9_(PWM)
  N19: LED10.cathode, R18.Pin_0
  N20: LED10.anode, U1.D8
  N21: S1.leg0, C2.+, U2.input_voltage
  N22: S1.leg1, VCC1.+
  N23: S2.2, C1.+, U1.VCC, U1.AVCC, U1.AREF, R12.Pin_0, LED11.anode, U2.output_voltage
  N24: S2.3, R25.Pin_0
  N25: S2.4, U1.D2
  N26: S3.2, U1.RESET, R12.Pin_1
  GND: S3.4, VCC1.-, C1.-, C2.-, U1.GND, R13.Pin_1, R14.Pin_1, R15.Pin_1, R16.Pin_1, R17.Pin_1, R18.Pin_1, R19.Pin_1, R20.Pin_1, R21.Pin_1, R22.Pin_1, C5.0, C6.0, R23.Pin_1, R24.Pin_1, R25.Pin_1, U2.GND
  N27: U1.XLAT1, XTAL1.pin_0, C5.1
  N28: U1.XLAT2, XTAL1.pin_1, C6.1
  N29: U1.D13, J1.pin2
  N30: LED11.cathode, R23.Pin_0
  N31: J1.pin1, R24.Pin_0
